# Fritzing sketch timer (saved by Fritzing 0.9.3b)
breadboards: 1

parts:
  Part1 = Arduino Uno (Rev3)
  S1 = Pushbutton [package=THT]
  S2 = Pushbutton [package=THT]
  IC1 = IC, SIP package, 5 pins [chip_label="7 seg"]

nets:
  N1: Part1.A5/SCL, IC1.pin1
  N2: Part1.D8, S2.leg0
  N3: Part1.D9_PWM, S1.leg0
  N4: Part1.GND, S1.leg1, S2.leg1, IC1.pin3
  N5: Part1.A4/SDA, IC1.pin2
  N6: Part1.5V, IC1.pin4, IC1.pin5
